// Logisim project 2107013_DLD_FINAL_PROJECT.circ as structural Verilog: 5 circuits, main circuit main
module main (
  input  Z,
  input  preset,
  input  clear
);

  wire and_1_out, and_2_out, and_3_out, and_4_out, and_5_out, and_6_out, and_7_out, and_8_out, and_9_out,
       and_10_out, bcd_to_7_segment_1_a_2, bcd_to_7_segment_1_b_2, bcd_to_7_segment_1_c_2,
       bcd_to_7_segment_1_d_2, bcd_to_7_segment_1_e, bcd_to_7_segment_1_f, bcd_to_7_segment_1_g,
       bcd_to_7_segment_2_a_2, bcd_to_7_segment_2_b_2, bcd_to_7_segment_2_c_2, bcd_to_7_segment_2_d_2,
       bcd_to_7_segment_2_e, bcd_to_7_segment_2_f, bcd_to_7_segment_2_g, bcd_to_7_segment_3_a_2,
       bcd_to_7_segment_3_b_2, bcd_to_7_segment_3_c_2, bcd_to_7_segment_3_d_2, bcd_to_7_segment_3_e,
       bcd_to_7_segment_3_f, bcd_to_7_segment_3_g, bcd_to_7_segment_4_a_2, bcd_to_7_segment_4_b_2,
       bcd_to_7_segment_4_c_2, bcd_to_7_segment_4_d_2, bcd_to_7_segment_4_e, bcd_to_7_segment_4_f,
       bcd_to_7_segment_4_g, bcd_to_7_segment_5_a_2, bcd_to_7_segment_5_b_2, bcd_to_7_segment_5_c_2,
       bcd_to_7_segment_5_d_2, bcd_to_7_segment_5_e, bcd_to_7_segment_5_f, bcd_to_7_segment_5_g,
       bcd_to_7_segment_6_a_2, bcd_to_7_segment_6_b_2, bcd_to_7_segment_6_c_2, bcd_to_7_segment_6_d_2,
       bcd_to_7_segment_6_e, bcd_to_7_segment_6_f, bcd_to_7_segment_6_g, clock_out, modulo_3_counter_1_t0,
       modulo_3_counter_1_t1, modulo_3_counter_1_t2, modulo_3_counter_1_t3, modulo_6_counter_1_q0,
       modulo_6_counter_1_q1, modulo_6_counter_1_q2, modulo_6_counter_1_q3, modulo_6_counter_2_q0,
       modulo_6_counter_2_q1, modulo_6_counter_2_q2, modulo_6_counter_2_q3, modulo_10_counter_1_t0,
       modulo_10_counter_1_t1, modulo_10_counter_1_t2, modulo_10_counter_1_t3, modulo_10_counter_2_t0,
       modulo_10_counter_2_t1, modulo_10_counter_2_t2, modulo_10_counter_2_t3, modulo_10_counter_3_t0,
       modulo_10_counter_3_t1, modulo_10_counter_3_t2, modulo_10_counter_3_t3, nor_1_out, nor_2_out,
       nor_3_out, not_1_out, not_2_out, not_3_out, or_1_out;

  not not_1 (not_1_out, modulo_3_counter_1_t0);
  nor nor_1 (nor_1_out, modulo_3_counter_1_t3, modulo_3_counter_1_t2, modulo_3_counter_1_t1, not_1_out);
  Clock clock (.out(clock_out));
  _7_Segment_Display u_7_segment_display_1 (
    .g(bcd_to_7_segment_1_g), .f(bcd_to_7_segment_1_f), .a(bcd_to_7_segment_1_a_2),
    .b(bcd_to_7_segment_1_b_2), .e(bcd_to_7_segment_1_e), .d(bcd_to_7_segment_1_d_2),
    .c(bcd_to_7_segment_1_c_2));  // open: dp
  modulo_3_counter modulo_3_counter_1 (
    .clock(clock_out), .preset(preset), .clear(clear), .z(or_1_out), .T0(modulo_3_counter_1_t0),
    .T1(modulo_3_counter_1_t1), .T2(modulo_3_counter_1_t2), .T3(modulo_3_counter_1_t3));
  or or_1 (or_1_out, and_3_out, and_2_out);
  BCD_to_7_segment bcd_to_7_segment_1 (
    .A(modulo_3_counter_1_t3), .B(modulo_3_counter_1_t2), .C(modulo_3_counter_1_t1),
    .D(modulo_3_counter_1_t0), .a_2(bcd_to_7_segment_1_a_2), .b_2(bcd_to_7_segment_1_b_2),
    .c_2(bcd_to_7_segment_1_c_2), .d_2(bcd_to_7_segment_1_d_2), .e(bcd_to_7_segment_1_e),
    .f(bcd_to_7_segment_1_f), .g(bcd_to_7_segment_1_g));
  and and_1 (and_1_out, modulo_10_counter_1_t1, modulo_10_counter_1_t0);
  and and_2 (and_2_out, modulo_10_counter_1_t3, and_5_out, modulo_10_counter_1_t0);
  and and_3 (and_3_out, and_1_out, and_5_out, modulo_3_counter_1_t1);
  _7_Segment_Display u_7_segment_display_2 (
    .g(bcd_to_7_segment_2_g), .f(bcd_to_7_segment_2_f), .a(bcd_to_7_segment_2_a_2),
    .b(bcd_to_7_segment_2_b_2), .e(bcd_to_7_segment_2_e), .d(bcd_to_7_segment_2_d_2),
    .c(bcd_to_7_segment_2_c_2));  // open: dp
  BCD_to_7_segment bcd_to_7_segment_2 (
    .A(modulo_10_counter_1_t3), .B(modulo_10_counter_1_t2), .C(modulo_10_counter_1_t1),
    .D(modulo_10_counter_1_t0), .a_2(bcd_to_7_segment_2_a_2), .b_2(bcd_to_7_segment_2_b_2),
    .c_2(bcd_to_7_segment_2_c_2), .d_2(bcd_to_7_segment_2_d_2), .e(bcd_to_7_segment_2_e),
    .f(bcd_to_7_segment_2_f), .g(bcd_to_7_segment_2_g));
  modulo_10_counter modulo_10_counter_1 (
    .x(nor_1_out), .clock(clock_out), .preset(preset), .clear(clear), .y(modulo_3_counter_1_t1),
    .T0(modulo_10_counter_1_t0), .T1(modulo_10_counter_1_t1), .T2(modulo_10_counter_1_t2),
    .T3(modulo_10_counter_1_t3), .z(and_5_out));
  and and_4 (and_4_out, and_6_out, and_7_out);
  and and_5 (and_5_out, and_4_out, and_8_out);
  LED led_1 (.in(1'b1));
  LED led_2 (.in(1'b1));
  and and_6 (and_6_out, modulo_6_counter_1_q2, modulo_6_counter_1_q0);
  _7_Segment_Display u_7_segment_display_3 (
    .g(bcd_to_7_segment_3_g), .f(bcd_to_7_segment_3_f), .a(bcd_to_7_segment_3_a_2),
    .b(bcd_to_7_segment_3_b_2), .e(bcd_to_7_segment_3_e), .d(bcd_to_7_segment_3_d_2),
    .c(bcd_to_7_segment_3_c_2));  // open: dp
  BCD_to_7_segment bcd_to_7_segment_3 (
    .A(modulo_6_counter_1_q3), .B(modulo_6_counter_1_q2), .C(modulo_6_counter_1_q1),
    .D(modulo_6_counter_1_q0), .a_2(bcd_to_7_segment_3_a_2), .b_2(bcd_to_7_segment_3_b_2),
    .c_2(bcd_to_7_segment_3_c_2), .d_2(bcd_to_7_segment_3_d_2), .e(bcd_to_7_segment_3_e),
    .f(bcd_to_7_segment_3_f), .g(bcd_to_7_segment_3_g));
  modulo_6_counter modulo_6_counter_1 (
    .clock(clock_out), .preset(preset), .clear(clear), .z(and_7_out), .Q0(modulo_6_counter_1_q0),
    .Q1(modulo_6_counter_1_q1), .Q2(modulo_6_counter_1_q2), .Q3(modulo_6_counter_1_q3));
  _7_Segment_Display u_7_segment_display_4 (
    .g(bcd_to_7_segment_4_g), .f(bcd_to_7_segment_4_f), .a(bcd_to_7_segment_4_a_2),
    .b(bcd_to_7_segment_4_b_2), .e(bcd_to_7_segment_4_e), .d(bcd_to_7_segment_4_d_2),
    .c(bcd_to_7_segment_4_c_2));  // open: dp
  and and_7 (and_7_out, modulo_10_counter_2_t3, and_8_out, modulo_10_counter_2_t0);
  not not_2 (not_2_out, modulo_6_counter_1_q0);
  nor nor_2 (nor_2_out, modulo_6_counter_1_q3, modulo_6_counter_1_q2, modulo_6_counter_1_q1, not_2_out);
  BCD_to_7_segment bcd_to_7_segment_4 (
    .A(modulo_10_counter_2_t3), .B(modulo_10_counter_2_t2), .C(modulo_10_counter_2_t1),
    .D(modulo_10_counter_2_t0), .a_2(bcd_to_7_segment_4_a_2), .b_2(bcd_to_7_segment_4_b_2),
    .c_2(bcd_to_7_segment_4_c_2), .d_2(bcd_to_7_segment_4_d_2), .e(bcd_to_7_segment_4_e),
    .f(bcd_to_7_segment_4_f), .g(bcd_to_7_segment_4_g));
  modulo_10_counter modulo_10_counter_2 (
    .x(nor_2_out), .clock(clock_out), .preset(preset), .clear(clear), .y(1'b0), .T0(modulo_10_counter_2_t0),
    .T1(modulo_10_counter_2_t1), .T2(modulo_10_counter_2_t2), .T3(modulo_10_counter_2_t3), .z(and_8_out));
  and and_8 (and_8_out, and_9_out, and_10_out);
  _7_Segment_Display u_7_segment_display_5 (
    .g(bcd_to_7_segment_5_g), .f(bcd_to_7_segment_5_f), .a(bcd_to_7_segment_5_a_2),
    .b(bcd_to_7_segment_5_b_2), .e(bcd_to_7_segment_5_e), .d(bcd_to_7_segment_5_d_2),
    .c(bcd_to_7_segment_5_c_2));  // open: dp
  LED led_3 (.in(1'b1));
  LED led_4 (.in(1'b1));
  modulo_6_counter modulo_6_counter_2 (
    .clock(clock_out), .preset(preset), .clear(clear), .z(and_10_out), .Q0(modulo_6_counter_2_q0),
    .Q1(modulo_6_counter_2_q1), .Q2(modulo_6_counter_2_q2), .Q3(modulo_6_counter_2_q3));
  and and_9 (and_9_out, modulo_6_counter_2_q2, modulo_6_counter_2_q0);
  BCD_to_7_segment bcd_to_7_segment_5 (
    .A(modulo_6_counter_2_q3), .B(modulo_6_counter_2_q2), .C(modulo_6_counter_2_q1),
    .D(modulo_6_counter_2_q0), .a_2(bcd_to_7_segment_5_a_2), .b_2(bcd_to_7_segment_5_b_2),
    .c_2(bcd_to_7_segment_5_c_2), .d_2(bcd_to_7_segment_5_d_2), .e(bcd_to_7_segment_5_e),
    .f(bcd_to_7_segment_5_f), .g(bcd_to_7_segment_5_g));
  and and_10 (and_10_out, modulo_10_counter_3_t3, Z, modulo_10_counter_3_t0);
  not not_3 (not_3_out, modulo_6_counter_2_q0);
  nor nor_3 (nor_3_out, modulo_6_counter_2_q3, modulo_6_counter_2_q2, modulo_6_counter_2_q1, not_3_out);
  _7_Segment_Display u_7_segment_display_6 (
    .g(bcd_to_7_segment_6_g), .f(bcd_to_7_segment_6_f), .a(bcd_to_7_segment_6_a_2),
    .b(bcd_to_7_segment_6_b_2), .e(bcd_to_7_segment_6_e), .d(bcd_to_7_segment_6_d_2),
    .c(bcd_to_7_segment_6_c_2));  // open: dp
  BCD_to_7_segment bcd_to_7_segment_6 (
    .A(modulo_10_counter_3_t3), .B(modulo_10_counter_3_t2), .C(modulo_10_counter_3_t1),
    .D(modulo_10_counter_3_t0), .a_2(bcd_to_7_segment_6_a_2), .b_2(bcd_to_7_segment_6_b_2),
    .c_2(bcd_to_7_segment_6_c_2), .d_2(bcd_to_7_segment_6_d_2), .e(bcd_to_7_segment_6_e),
    .f(bcd_to_7_segment_6_f), .g(bcd_to_7_segment_6_g));
  modulo_10_counter modulo_10_counter_3 (
    .x(nor_3_out), .clock(clock_out), .preset(preset), .clear(clear), .y(1'b0), .T0(modulo_10_counter_3_t0),
    .T1(modulo_10_counter_3_t1), .T2(modulo_10_counter_3_t2), .T3(modulo_10_counter_3_t3), .z(Z));

  // Notes on the sheet:
  //   HOUR
  //   DIGITAL   CLOCK
  //   -------------------------
  //   MINUTE
  //   SECOND
  //   Y
  //   ROLL: 2107013
  //   ROLL: 2107014
endmodule

module modulo_10_counter (
  input  x,
  input  y,
  input  clock,
  input  preset,
  input  z,
  input  clear,
  output T0,
  output T1,
  output T2,
  output T3
);

  wire A_qn, and_1_out, and_2_out, and_3_out, and_4_out, and_5_out, and_6_out, and_7_out, and_8_out,
       and_9_out, and_10_out, and_11_out, and_12_out, and_13_out, and_14_out, and_15_out, and_16_out, B_qn,
       C_qn, not_1_out, not_2_out, or_1_out, or_2_out, or_3_out, or_4_out, or_5_out, or_6_out, or_7_out;

  or or_1 (or_1_out, T2, not_1_out, C_qn);
  not not_1 (not_1_out, x);
  T_Flip_Flop D (.clk(clock), .T(and_1_out), .Q(T0), .preset(preset), .reset(clear));  // open: Qn, en
  and and_1 (and_1_out, z, or_6_out);
  and and_2 (and_2_out, or_4_out, not_2_out);
  and and_3 (and_3_out, T0, y);
  and and_4 (and_4_out, x, B_qn, T1);
  or or_2 (or_2_out, and_2_out, and_3_out);
  or or_3 (or_3_out, and_4_out, and_6_out);
  T_Flip_Flop C (.clk(clock), .T(and_9_out), .Q(T1), .Qn(C_qn), .preset(preset), .reset(clear));  // open: en
  or or_4 (or_4_out, and_4_out, and_5_out);
  and and_5 (and_5_out, T0, A_qn);
  and and_6 (and_6_out, T0, T1);
  or or_5 (or_5_out, and_8_out, and_7_out);
  and and_7 (and_7_out, not_2_out, or_3_out);
  and and_8 (and_8_out, y, 1'b0);
  and and_9 (and_9_out, or_2_out, z);
  and and_10 (and_10_out, not_2_out, or_1_out);
  and and_11 (and_11_out, y, 1'b1);
  T_Flip_Flop B (.clk(clock), .T(and_15_out), .Q(T2), .Qn(B_qn), .preset(preset), .reset(clear));  // open: en
  or or_6 (or_6_out, and_10_out, and_11_out);
  and and_12 (and_12_out, T0, T3);
  and and_13 (and_13_out, and_6_out, T2);
  and and_14 (and_14_out, z, and_16_out);
  and and_15 (and_15_out, or_5_out, z);
  or or_7 (or_7_out, and_12_out, and_13_out);
  T_Flip_Flop A (.clk(clock), .T(and_14_out), .Q(T3), .Qn(A_qn), .preset(preset), .reset(clear));  // open: en
  not not_2 (not_2_out, y);
  and and_16 (and_16_out, or_7_out, not_2_out);

  // Notes on the sheet:
  //   ROLL: 2107014
endmodule

module modulo_6_counter (
  input  clock,
  input  preset,
  input  clear,
  input  z,
  output Q0,
  output Q1,
  output Q2,
  output Q3
);

  wire and_1_out, and_2_out, and_3_out, and_4_out, and_5_out, and_6_out, and_7_out, J2_K2_qn;

  and and_1 (and_1_out, z, and_3_out);
  and and_2 (and_2_out, 1'b1, z);
  and and_3 (and_3_out, J2_K2_qn, Q0);
  J_K_Flip_Flop J0_K0 (
    .J(and_2_out), .clk(clock), .K(and_2_out), .Q(Q0), .preset(preset), .reset(clear));  // open: Qn, en
  J_K_Flip_Flop J1_K1 (
    .J(and_1_out), .clk(clock), .K(and_4_out), .Q(Q1), .preset(preset), .reset(clear));  // open: Qn, en
  and and_4 (and_4_out, Q0, z);
  and and_5 (and_5_out, z, and_6_out);
  and and_6 (and_6_out, Q0, Q1);
  J_K_Flip_Flop J2_K2 (
    .J(and_5_out), .clk(clock), .K(and_7_out), .Q(Q2), .Qn(J2_K2_qn), .preset(preset), .reset(clear));  // open: en
  and and_7 (and_7_out, Q0, z);

  assign Q3 = 1'b0;

  // Notes on the sheet:
  //   ROLL: 2107013
endmodule

module BCD_to_7_segment (
  input  A,
  input  B,
  input  C,
  input  D,
  output a_2,
  output b_2,
  output c_2,
  output d_2,
  output e,
  output f,
  output g
);

  wire A_prime_out, and_1_out, and_2_out, and_3_out, and_4_out, and_5_out, and_6_out, and_7_out, and_8_out,
       and_9_out, and_10_out, and_11_out, and_12_out, and_13_out, and_14_out, and_15_out, B_prime_out,
       C_prime_out, D_prime_out, or_1_out;

  not A_prime (A_prime_out, A);
  not B_prime (B_prime_out, B);
  not C_prime (C_prime_out, C);
  not D_prime (D_prime_out, D);
  or or_1 (or_1_out, C_prime_out, D_prime_out);
  and and_1 (and_1_out, B, D);
  and and_2 (and_2_out, B_prime_out, D_prime_out);
  and and_3 (and_3_out, C_prime_out, D_prime_out);
  and and_4 (and_4_out, C, D);
  and and_5 (and_5_out, B_prime_out, C);
  and and_6 (and_6_out, C, D_prime_out);
  and and_7 (and_7_out, B_prime_out, D_prime_out);
  and and_8 (and_8_out, B, C_prime_out, D);
  and and_9 (and_9_out, B_prime_out, D_prime_out);
  and and_10 (and_10_out, C, D_prime_out);
  and and_11 (and_11_out, C_prime_out, D_prime_out);
  and and_12 (and_12_out, or_1_out, B);
  and and_13 (and_13_out, B, C_prime_out);
  and and_14 (and_14_out, B_prime_out, C);
  and and_15 (and_15_out, C, D_prime_out);
  or or_2 (a_2, and_1_out, and_2_out, A, C);
  or or_3 (b_2, and_3_out, and_4_out, B_prime_out);
  or or_4 (c_2, B, C_prime_out, D);
  or or_5 (d_2, and_5_out, and_6_out, and_7_out, and_8_out, A);
  or or_6 (e, and_9_out, and_10_out);
  or or_7 (f, and_11_out, and_12_out, A);
  or or_8 (g, and_13_out, and_14_out, and_15_out, A);

  // Notes on the sheet:
  //   ROLL: 2107014
endmodule

module modulo_3_counter (
  input  clock,
  input  preset,
  input  clear,
  input  z,
  output T0,
  output T1,
  output T2,
  output T3
);

  wire A_qn, and_1_out, and_2_out, or_1_out;

  and and_1 (and_1_out, z, A_qn);
  T_Flip_Flop B (.clk(clock), .T(and_1_out), .Q(T0), .preset(preset), .reset(clear));  // open: Qn, en
  and and_2 (and_2_out, z, or_1_out);
  or or_1 (or_1_out, T1, T0);
  T_Flip_Flop A (.clk(clock), .T(and_2_out), .Q(T1), .Qn(A_qn), .preset(preset), .reset(clear));  // open: en

  assign T2 = 1'b0;
  assign T3 = 1'b0;

  // Notes on the sheet:
  //   ROLL: 2107013
endmodule
